# Fritzing sketch oled (saved by Fritzing 1.0.3b)
breadboards: 1

parts:
  Componente1 = Caytan Enterprise Micro:bit Tail
  OLED_I2C1 = OLED 128x64 I2C Monochrome Display
  DFRobot_DFPlayer_Mini1 = DFRobot DFPlayer Mini [part_number=DFR0299]
  J2 = Basic Servo

nets:
  GND: Componente1.GND, OLED_I2C1.GND, DFRobot_DFPlayer_Mini1.GND-1, DFRobot_DFPlayer_Mini1.GND-2, J2.gnd
  N1: Componente1.P0, J2.pulse
  N2: Componente1.P1, DFRobot_DFPlayer_Mini1.RX
  N3: Componente1.P2, DFRobot_DFPlayer_Mini1.TX
  VCC: Componente1.3.3V, OLED_I2C1.VDD, DFRobot_DFPlayer_Mini1.VCC, J2.vcc
  N4: Componente1.P20, OLED_I2C1.SDA
  N5: Componente1.P13, OLED_I2C1.SCK

custom parts:
  Caytan Enterprise Micro:bit Tail: This breakout board has the edge connector for your micro:bit, allowing access to all of the pins available.
